// Logisim project Multiplier.circ as structural Verilog: 1 circuit, main circuit main
module main (
  input  [7:0] Multiplicand_Init,
  input  Load,
  input  [7:0] Multiplier_Init,
  output [3:0] out_4,
  output [7:0] Result,
  output Completed
);

  wire Clock_out, not_1_out, not_2_out;
  wire [3:0] adder_1_out;
  wire [7:0] adder_2_out, multiplexer_1_out, multiplexer_2_out, multiplexer_3_out, Multiplicand_q,
       Multiplier_q, shifter_1_out, shifter_2_out;

  Clock Clock (.out(Clock_out));
  Multiplexer #(.width(8), .enable("false")) multiplexer_1 (
    .in0(shifter_1_out), .in1(Multiplicand_Init), .out(multiplexer_1_out), .sel(Load));
  Multiplexer #(.width(8), .enable("false")) multiplexer_2 (
    .in0(shifter_2_out), .in1(Multiplier_Init), .out(multiplexer_2_out), .sel(Load));
  not not_1 (not_1_out, Completed);
  Register Multiplicand (.D(multiplexer_1_out), .Q(Multiplicand_q), .clk(Clock_out));  // open: en, clr
  Register Multiplier (.D(multiplexer_2_out), .Q(Multiplier_q), .clk(Clock_out));  // open: en, clr
  Register u_Result (.D(adder_2_out), .en(not_1_out), .Q(Result), .clk(Clock_out), .clr(Load));
  Shifter shifter_1 (.in(Multiplicand_q), .\dist (3'b001), .out(shifter_1_out));
  Shifter #(.shift("lr")) shifter_2 (.in(Multiplier_q), .\dist (3'b001), .out(shifter_2_out));
  not not_2 (not_2_out, Completed);
  Register #(.width(4)) Counter (.D(adder_1_out), .en(not_2_out), .Q(out_4), .clk(Clock_out), .clr(Load));
  Multiplexer #(.width(8), .enable("false")) multiplexer_3 (
    .in0({8{1'b0}}), .in1(Multiplicand_q), .out(multiplexer_3_out), .sel(Multiplier_q[0]));
  Adder #(.width(4)) adder_1 (.a(out_4), .b(4'b0001), .out(adder_1_out), .cin(1'b0));  // open: cout
  Adder adder_2 (.a(multiplexer_3_out), .b(Result), .out(adder_2_out), .cin(1'b0));  // open: cout
  Comparator #(.width(4)) comparator_1 (.a(out_4), .b(4'b1000), .eq(Completed));  // open: gt, lt
endmodule
