// Logisim project processor.circ as structural Verilog: 8 circuits, main circuit main
module main (
  input  Clear,
  output [7:0] out_2,
  output [7:0] out_3,
  output [7:0] PC
);

  wire alu_1_zero, and_1_out, and_2_out, Clock_out, control_unit_1_alusrc, control_unit_1_branch_equal,
       control_unit_1_branch_not_equal, control_unit_1_cin, control_unit_1_jump, control_unit_1_memread,
       control_unit_1_memtoreg, control_unit_1_memwrite, control_unit_1_regdst, control_unit_1_regwrite,
       control_unit_1_s0, control_unit_1_s1, control_unit_1_s2, control_unit_1_shift_left,
       control_unit_1_shift_right, not_1_out, or_1_out;
  wire [3:0] alu_1_s, data_memory_1_out, instruction_memory_1__0_3, instruction_memory_1__4_7,
       instruction_memory_1__8_11, instruction_memory_1__12_15, multiplexer_1_out, multiplexer_3_out,
       multiplexer_5_out, register_file_1_read_1, register_file_1_read_2;
  wire [7:0] adder_1_out, bit_extender_1_out, bit_extender_2_out, instruction_memory_1__4_11,
       multiplexer_4_out;

  Clock Clock (.out(Clock_out));
  Program_Counter program_counter_1 (.In(multiplexer_4_out), .Clock(Clock_out), .Clear(Clear), .PC(PC));
  Instruction_Memory instruction_memory_1 (
    .Address(PC), ._12_15(instruction_memory_1__12_15), ._8_11(instruction_memory_1__8_11),
    ._4_7(instruction_memory_1__4_7), ._0_3(instruction_memory_1__0_3), ._4_11(instruction_memory_1__4_11));  // open: Instruction
  assign bit_extender_1_out = {{4{instruction_memory_1__0_3[3]}}, instruction_memory_1__0_3};  // Bit_Extender bit_extender_1
  Adder adder_1 (.a(PC), .b(bit_extender_1_out), .out(adder_1_out), .cin(1'b0));  // open: cout
  Control_Unit control_unit_1 (
    .Opcode(instruction_memory_1__12_15), .Shift_Right(control_unit_1_shift_right),
    .Shift_Left(control_unit_1_shift_left), .Cin(control_unit_1_cin), .s0(control_unit_1_s0),
    .s1(control_unit_1_s1), .s2(control_unit_1_s2), .MemWrite(control_unit_1_memwrite),
    .MemRead(control_unit_1_memread), .Jump(control_unit_1_jump),
    .Branch_Not_Equal(control_unit_1_branch_not_equal), .Branch_Equal(control_unit_1_branch_equal),
    .RegWrite(control_unit_1_regwrite), .MemToReg(control_unit_1_memtoreg), .ALUSrc(control_unit_1_alusrc),
    .RegDst(control_unit_1_regdst));
  Adder adder_2 (.a(PC), .b(8'h1), .out(out_3), .cin(1'b0));  // open: cout
  Multiplexer #(.width(4)) multiplexer_1 (
    .in0(instruction_memory_1__4_7), .in1(instruction_memory_1__0_3), .out(multiplexer_1_out),
    .sel(control_unit_1_regdst), .en(1'b1));
  Register_File register_file_1 (
    .RegWrite(control_unit_1_regwrite), .Reg1(instruction_memory_1__8_11), .Reg2(instruction_memory_1__4_7),
    .WriteReg(multiplexer_1_out), .Data(multiplexer_5_out), .Clock(Clock_out), .Clear(Clear),
    .Read_1(register_file_1_read_1), .Read_2(register_file_1_read_2));
  Multiplexer #(.width(8)) multiplexer_2 (.in0(out_3), .in1(adder_1_out), .out(out_2), .sel(or_1_out), .en(1'b1));
  Multiplexer #(.width(4)) multiplexer_3 (
    .in0(register_file_1_read_2), .in1(instruction_memory_1__0_3), .out(multiplexer_3_out),
    .sel(control_unit_1_alusrc), .en(1'b1));
  or or_1 (or_1_out, and_1_out, and_2_out);
  and and_1 (and_1_out, control_unit_1_branch_equal, alu_1_zero);
  ALU alu_1 (
    .A(register_file_1_read_1), .B(multiplexer_3_out), .S(alu_1_s), .s2(control_unit_1_s2),
    .s1(control_unit_1_s1), .s0(control_unit_1_s0), .Cin(control_unit_1_cin),
    .ShiftLeft(control_unit_1_shift_left), .ShiftRight(control_unit_1_shift_right), .Zero(alu_1_zero));
  Multiplexer #(.width(8)) multiplexer_4 (
    .in0(out_2), .in1(instruction_memory_1__4_11), .out(multiplexer_4_out), .sel(control_unit_1_jump),
    .en(1'b1));
  and and_2 (and_2_out, not_1_out, control_unit_1_branch_not_equal);
  not not_1 (not_1_out, alu_1_zero);
  assign bit_extender_2_out = {{4{1'b0}}, alu_1_s};  // Bit_Extender bit_extender_2
  Data_Memory data_memory_1 (
    .Address(bit_extender_2_out), .Data(register_file_1_read_2), .MemWrite(control_unit_1_memwrite),
    .Clock(Clock_out), .MemRead(control_unit_1_memread), .Clear(Clear), .Out(data_memory_1_out));
  Multiplexer #(.width(4)) multiplexer_5 (
    .in0(alu_1_s), .in1(data_memory_1_out), .out(multiplexer_5_out), .sel(control_unit_1_memtoreg), .en(1'b1));

  // Notes on the sheet:
  //   PC+1
  //   branch
  //   jump address
endmodule

// PC
module Program_Counter (
  input  [7:0] In,
  input  Clock,
  input  Clear,
  output [7:0] PC
);

  Register register_1 (.D(In), .en(1'b1), .Q(PC), .clk(Clock), .clr(Clear));
endmodule

// IM
module Instruction_Memory (
  input  [7:0] Address,
  output [3:0] _12_15,
  output [3:0] _8_11,
  output [3:0] _4_7,
  output [3:0] _0_3,
  output [7:0] _4_11,
  output [15:0] Instruction
);

  ROM #(.dataWidth(16)) rom_1 (.addr(Address), .data({_12_15, _4_11[7:4], _4_7, _0_3}), .sel(1'b1));

  assign _4_11[3:0] = _4_7;
  assign _8_11 = _4_11[7:4];
  assign Instruction = {_12_15, _4_11[7:4], _4_7, _0_3};

  // Notes on the sheet:
  //   contents of rom_1 (hex, n*v repeats v):
  //   3017 3027 f123 3030 c060 3031 8303
endmodule

// RF
module Register_File (
  input  RegWrite,
  input  [3:0] Reg1,
  input  [3:0] Reg2,
  input  [3:0] WriteReg,
  input  [3:0] Data,
  input  Clock,
  input  Clear,
  output [3:0] Read_1,
  output [3:0] Read_2
);

  wire and_1_out, and_2_out, and_3_out, and_4_out, and_5_out, and_6_out, and_7_out, and_8_out,
       decoder_1_out0, decoder_1_out1, decoder_1_out2, decoder_1_out3, decoder_1_out4, decoder_1_out5,
       decoder_1_out6, decoder_1_out7;
  wire [3:0] register_1_q, register_2_q, t0_q, t1_q, t2_q, t3_q, t4_q, Zero_q;

  Decoder #(.select(3)) decoder_1 (
    .out0(decoder_1_out0), .out1(decoder_1_out1), .out2(decoder_1_out2), .out3(decoder_1_out3),
    .out4(decoder_1_out4), .out5(decoder_1_out5), .out6(decoder_1_out6), .out7(decoder_1_out7),
    .sel(WriteReg[2:0]), .en(1'b1));
  and and_1 (and_1_out, RegWrite, decoder_1_out0);
  and and_2 (and_2_out, RegWrite, decoder_1_out1);
  and and_3 (and_3_out, RegWrite, decoder_1_out2);
  and and_4 (and_4_out, RegWrite, decoder_1_out3);
  and and_5 (and_5_out, RegWrite, decoder_1_out4);
  and and_6 (and_6_out, RegWrite, decoder_1_out5);
  and and_7 (and_7_out, RegWrite, decoder_1_out6);
  and and_8 (and_8_out, RegWrite, decoder_1_out7);
  Register #(.width(4)) Zero (.D(4'b0000), .en(and_1_out), .Q(Zero_q), .clk(Clock), .clr(Clear));
  Register #(.width(4)) t0 (.D(Data), .en(and_2_out), .Q(t0_q), .clk(Clock), .clr(Clear));
  Register #(.width(4)) t1 (.D(Data), .en(and_3_out), .Q(t1_q), .clk(Clock), .clr(Clear));
  Register #(.width(4)) t2 (.D(Data), .en(and_4_out), .Q(t2_q), .clk(Clock), .clr(Clear));
  Register #(.width(4)) t3 (.D(Data), .en(and_5_out), .Q(t3_q), .clk(Clock), .clr(Clear));
  Register #(.width(4)) t4 (.D(Data), .en(and_6_out), .Q(t4_q), .clk(Clock), .clr(Clear));
  Register #(.width(4)) register_1 (.D(Data), .en(and_7_out), .Q(register_1_q), .clk(Clock), .clr(Clear));
  Register #(.width(4)) register_2 (.D(Data), .en(and_8_out), .Q(register_2_q), .clk(Clock), .clr(Clear));
  Multiplexer #(.select(3), .width(4)) multiplexer_1 (
    .in0(Zero_q), .in1(t0_q), .in2(t1_q), .in3(t2_q), .in4(t3_q), .in5(t4_q), .in6(register_1_q),
    .in7(register_2_q), .out(Read_1), .sel(Reg1[2:0]), .en(1'b1));
  Multiplexer #(.select(3), .width(4)) multiplexer_2 (
    .in0(Zero_q), .in1(t0_q), .in2(t1_q), .in3(t2_q), .in4(t3_q), .in5(t4_q), .in6(register_1_q),
    .in7(register_2_q), .out(Read_2), .sel(Reg2[2:0]), .en(1'b1));
endmodule

// DM
module Data_Memory (
  input  [7:0] Address,
  input  [3:0] Data,
  input  MemWrite,
  input  Clock,
  input  MemRead,
  input  Clear,
  output [3:0] Out
);

  RAM #(.dataWidth(4), .bus("separate")) ram_1 (
    .addr(Address), .din(Data), .data(Out), .str(MemWrite), .sel(1'b1), .clk(Clock), .ld(MemRead), .clr(Clear));
endmodule

module ALU (
  input  s2,
  input  s1,
  input  s0,
  input  Cin,
  input  ShiftLeft,
  input  ShiftRight,
  input  [3:0] A,
  input  [3:0] B,
  output [3:0] S,
  output Zero
);

  wire adder_1_cout, adder_2_cout, adder_3_cout, alu_adder_module_1_xi, alu_adder_module_1_yi,
       alu_adder_module_1_zi, alu_adder_module_2_xi, alu_adder_module_2_yi, alu_adder_module_2_zi,
       alu_adder_module_3_xi, alu_adder_module_3_yi, alu_adder_module_3_zi, alu_adder_module_4_xi,
       alu_adder_module_4_yi, alu_adder_module_4_zi;
  wire [3:0] adder_1_out, multiplexer_1_out, shifter_1_out, shifter_2_out;

  ALU_Adder_Module alu_adder_module_1 (
    .s2(s2), .s1(s1), .s0(s0), .Ai(A[0]), .Bi(B[0]), .Ci(Cin), .Xi(alu_adder_module_1_xi),
    .Yi(alu_adder_module_1_yi), .Zi(alu_adder_module_1_zi));
  ALU_Adder_Module alu_adder_module_2 (
    .s2(s2), .s1(s1), .s0(s0), .Ai(A[1]), .Bi(B[1]), .Ci(adder_1_cout), .Xi(alu_adder_module_2_xi),
    .Yi(alu_adder_module_2_yi), .Zi(alu_adder_module_2_zi));
  ALU_Adder_Module alu_adder_module_3 (
    .s2(s2), .s1(s1), .s0(s0), .Ai(A[2]), .Bi(B[2]), .Ci(adder_2_cout), .Xi(alu_adder_module_3_xi),
    .Yi(alu_adder_module_3_yi), .Zi(alu_adder_module_3_zi));
  ALU_Adder_Module alu_adder_module_4 (
    .s2(s2), .s1(s1), .s0(s0), .Ai(A[3]), .Bi(B[3]), .Ci(adder_3_cout), .Xi(alu_adder_module_4_xi),
    .Yi(alu_adder_module_4_yi), .Zi(alu_adder_module_4_zi));
  Adder #(.width(1)) adder_1 (
    .a(alu_adder_module_1_xi), .b(alu_adder_module_1_yi), .out(adder_1_out[0]), .cin(alu_adder_module_1_zi),
    .cout(adder_1_cout));
  Adder #(.width(1)) adder_2 (
    .a(alu_adder_module_2_xi), .b(alu_adder_module_2_yi), .out(adder_1_out[1]), .cin(alu_adder_module_2_zi),
    .cout(adder_2_cout));
  Adder #(.width(1)) adder_3 (
    .a(alu_adder_module_3_xi), .b(alu_adder_module_3_yi), .out(adder_1_out[2]), .cin(alu_adder_module_3_zi),
    .cout(adder_3_cout));
  Adder #(.width(1)) adder_4 (
    .a(alu_adder_module_4_xi), .b(alu_adder_module_4_yi), .out(adder_1_out[3]), .cin(alu_adder_module_4_zi));  // open: cout
  nor nor_1 (Zero, S[0], S[1], S[2], S[3]);
  Shifter #(.width(4)) shifter_1 (.in(A), .\dist (B[1:0]), .out(shifter_1_out));
  Shifter #(.width(4), .shift("lr")) shifter_2 (.in(A), .\dist (B[1:0]), .out(shifter_2_out));
  Multiplexer #(.width(4)) multiplexer_1 (
    .in0(adder_1_out), .in1(shifter_1_out), .out(multiplexer_1_out), .sel(ShiftLeft), .en(1'b1));
  Multiplexer #(.width(4)) multiplexer_2 (
    .in0(multiplexer_1_out), .in1(shifter_2_out), .out(S), .sel(ShiftRight), .en(1'b1));

  // Notes on the sheet:
  //   A0
  //   B0
  //   A1
  //   A2
  //   B2
  //   A3
  //   B3
  //   B
  //   Zero Flag
  //   S0
  //   S1
  //   S2
  //   S3
  //   A
  //   Arithmetic Output
  //   Final Output
  //   shiftLeft
  //   shiftRight
endmodule

// Add_Module
module ALU_Adder_Module (
  input  s2,
  input  s1,
  input  s0,
  input  Ai,
  input  Bi,
  input  Ci,
  output Xi,
  output Yi,
  output Zi
);

  wire and_1_out, and_2_out, and_4_out, and_5_out, and_6_out, not_1_out, not_2_out, not_3_out, or_1_out,
       xor_1_out;

  not not_1 (not_1_out, s2);
  not not_2 (not_2_out, s1);
  not not_3 (not_3_out, Bi);
  and and_1 (and_1_out, s1, Bi);
  and and_2 (and_2_out, s0, not_2_out, not_3_out);
  or or_1 (or_1_out, and_1_out, and_2_out);
  xor xor_1 (xor_1_out, s0, Bi);
  and and_3 (Zi, Ci, not_1_out);
  and and_4 (and_4_out, or_1_out, s2);
  and and_5 (and_5_out, xor_1_out, not_2_out);
  and and_6 (and_6_out, s1, s0);
  or or_2 (Xi, and_4_out, Ai);
  or or_3 (Yi, and_5_out, and_6_out);
endmodule

module Control_Unit (
  input  [3:0] Opcode,
  output Shift_Right,
  output Shift_Left,
  output Cin,
  output s0,
  output s1,
  output s2,
  output MemWrite,
  output MemRead,
  output Jump,
  output Branch_Not_Equal,
  output Branch_Equal,
  output RegWrite,
  output MemToReg,
  output ALUSrc,
  output RegDst
);

  wire [0:0] rom_1_data;

  ROM #(.addrWidth(4), .dataWidth(16)) rom_1 (
    .addr(Opcode),
    .data({RegDst, ALUSrc, MemToReg, RegWrite, Branch_Equal, Branch_Not_Equal, Jump, MemRead, MemWrite, s2, s1, s0, Cin, Shift_Left, Shift_Right, rom_1_data[0]}),
    .sel(1'b1));

  // Notes on the sheet:
  //   contents of rom_1 (hex, n*v repeats v):
  //   9018 5004 4080 5000 7100 9050 5060 5018 9000 9060 418 5002 200 9070 5050 818
endmodule
